// Logisim project control-logic.circ as structural Verilog: 1 circuit, main circuit control_logic
module control_logic (
  input  [31:0] Instruction,
  input  BrEq,
  input  BrLt,
  output PCSel,
  output RegWEn,
  output [2:0] ImmSel,
  output BrUn,
  output ASel,
  output BSel,
  output [3:0] ALUSel,
  output MemWEn,
  output [1:0] WBSel
);

  wire and_4_out, and_5_out, and_6_out, and_7_out, and_8_out, and_9_out, comparator_1_eq, comparator_2_eq,
       comparator_3_eq, comparator_4_eq, comparator_5_eq, comparator_6_eq, comparator_7_eq, comparator_8_eq,
       comparator_9_eq, comparator_10_eq, comparator_11_eq, comparator_12_eq, comparator_13_eq,
       comparator_14_eq, comparator_15_eq, comparator_16_eq, comparator_17_eq, comparator_18_eq,
       comparator_19_eq, comparator_20_eq, comparator_21_eq, comparator_22_eq, comparator_23_eq,
       comparator_24_eq, comparator_25_eq, comparator_29_eq, comparator_30_eq, comparator_31_eq,
       comparator_32_eq, comparator_33_eq, comparator_34_eq, comparator_35_eq, is_mul, is_mulh, is_mulhu,
       is_sra, is_sub, not_1_out, not_2_out, not_3_out, or_2_out, or_3_out, or_5_out;
  wire [3:0] multiplexer_1_out, multiplexer_2_out, multiplexer_3_out, multiplexer_4_out, multiplexer_5_out,
       RISel;

  Multiplexer #(.enable("false"), .select(3), .width(4)) multiplexer_1 (
    .in0(4'b0000), .in1(4'b0001), .in2(4'b0010), .in4(4'b0100), .in5(4'b0101), .in6(4'b0110), .in7(4'b0111),
    .out(multiplexer_1_out), .sel(Instruction[14:12]));  // open: in3
  Multiplexer #(.enable("false"), .width(4)) multiplexer_2 (
    .in0(multiplexer_1_out), .in1(4'b1000), .out(multiplexer_2_out), .sel(is_mul));
  Comparator #(.width(7)) comparator_1 (.a(Instruction[6:0]), .b(7'b0110011), .eq(comparator_1_eq));  // open: gt, lt
  Comparator #(.width(7)) comparator_2 (.a(Instruction[6:0]), .b(7'b0000011), .eq(comparator_2_eq));  // open: gt, lt
  Comparator #(.width(7)) comparator_3 (.a(Instruction[6:0]), .b(7'b0010011), .eq(comparator_3_eq));  // open: gt, lt
  Comparator #(.width(7)) comparator_4 (.a(Instruction[6:0]), .b(7'b1100111), .eq(comparator_4_eq));  // open: gt, lt
  Comparator #(.width(7)) comparator_5 (.a(Instruction[6:0]), .b(7'b0010111), .eq(comparator_5_eq));  // open: gt, lt
  Comparator #(.width(7)) comparator_6 (.a(Instruction[6:0]), .b(7'b0110111), .eq(comparator_6_eq));  // open: gt, lt
  Comparator #(.width(7)) comparator_7 (.a(Instruction[6:0]), .b(7'b1101111), .eq(comparator_7_eq));  // open: gt, lt
  Comparator #(.width(7)) comparator_8 (.a(Instruction[6:0]), .b(7'b1100011), .eq(comparator_8_eq));  // open: gt, lt
  Comparator #(.width(3)) comparator_9 (.a(Instruction[14:12]), .b(3'b000), .eq(comparator_9_eq));  // open: gt, lt
  Comparator #(.width(3)) comparator_10 (.a(Instruction[14:12]), .b(3'b001), .eq(comparator_10_eq));  // open: gt, lt
  Comparator #(.width(3)) comparator_11 (.a(Instruction[14:12]), .b(3'b100), .eq(comparator_11_eq));  // open: gt, lt
  Comparator #(.width(3)) comparator_12 (.a(Instruction[14:12]), .b(3'b101), .eq(comparator_12_eq));  // open: gt, lt
  Comparator #(.width(3)) comparator_13 (.a(Instruction[14:12]), .b(3'b110), .eq(comparator_13_eq));  // open: gt, lt
  Comparator #(.width(3)) comparator_14 (.a(Instruction[14:12]), .b(3'b111), .eq(comparator_14_eq));  // open: gt, lt
  Multiplexer #(.enable("false"), .width(4)) multiplexer_3 (
    .in0(multiplexer_2_out), .in1(4'b1001), .out(multiplexer_3_out), .sel(is_mulh));
  Multiplexer #(.enable("false"), .width(4)) multiplexer_4 (
    .in0(multiplexer_3_out), .in1(4'b1011), .out(multiplexer_4_out), .sel(is_mulhu));
  Comparator #(.width(7)) comparator_15 (.a(Instruction[6:0]), .b(7'b0110011), .eq(comparator_15_eq));  // open: gt, lt
  Comparator #(.width(3)) comparator_16 (.a(Instruction[14:12]), .b(3'b000), .eq(comparator_16_eq));  // open: gt, lt
  Comparator #(.width(7)) comparator_17 (
    .a(Instruction[31:25]), .b(7'b0000001), .eq(comparator_17_eq));  // open: gt, lt
  Comparator #(.width(7)) comparator_18 (.a(Instruction[6:0]), .b(7'b0110011), .eq(comparator_18_eq));  // open: gt, lt
  Comparator #(.width(3)) comparator_19 (.a(Instruction[14:12]), .b(3'b001), .eq(comparator_19_eq));  // open: gt, lt
  Comparator #(.width(7)) comparator_20 (
    .a(Instruction[31:25]), .b(7'b0000001), .eq(comparator_20_eq));  // open: gt, lt
  Comparator #(.width(7)) comparator_21 (.a(Instruction[6:0]), .b(7'b0110011), .eq(comparator_21_eq));  // open: gt, lt
  Comparator #(.width(3)) comparator_22 (.a(Instruction[14:12]), .b(3'b011), .eq(comparator_22_eq));  // open: gt, lt
  Comparator #(.width(7)) comparator_23 (
    .a(Instruction[31:25]), .b(7'b0000001), .eq(comparator_23_eq));  // open: gt, lt
  or or_1 (RegWEn, comparator_1_eq, comparator_2_eq, comparator_3_eq, comparator_4_eq, comparator_5_eq, comparator_6_eq, comparator_7_eq);
  not not_1 (not_1_out, BrEq);
  not not_2 (not_2_out, BrLt);
  not not_3 (not_3_out, BrLt);
  Multiplexer #(.enable("false"), .width(4)) multiplexer_5 (
    .in0(multiplexer_4_out), .in1(4'b1100), .out(multiplexer_5_out), .sel(is_sub));
  and and_1 (is_mul, comparator_15_eq, comparator_16_eq, comparator_17_eq);
  and and_2 (is_mulh, comparator_18_eq, comparator_19_eq, comparator_20_eq);
  and and_3 (is_mulhu, comparator_21_eq, comparator_22_eq, comparator_23_eq);
  and and_4 (and_4_out, comparator_8_eq, comparator_9_eq, BrEq);
  and and_5 (and_5_out, comparator_8_eq, comparator_10_eq, not_1_out);
  and and_6 (and_6_out, comparator_8_eq, comparator_11_eq, BrLt);
  and and_7 (and_7_out, comparator_8_eq, comparator_12_eq, BrLt);
  and and_8 (and_8_out, comparator_8_eq, comparator_13_eq, not_2_out);
  and and_9 (and_9_out, comparator_8_eq, comparator_14_eq, not_3_out);
  Comparator #(.width(7)) comparator_24 (.a(Instruction[6:0]), .b(7'b1100111), .eq(comparator_24_eq));  // open: gt, lt
  Comparator #(.width(7)) comparator_25 (.a(Instruction[6:0]), .b(7'b1101111), .eq(comparator_25_eq));  // open: gt, lt
  Multiplexer #(.enable("false"), .width(4)) multiplexer_6 (
    .in0(multiplexer_5_out), .in1(4'b1101), .out(RISel), .sel(is_sra));
  or or_2 (or_2_out, and_4_out, and_5_out, and_6_out, and_7_out, and_8_out, and_9_out);
  or or_3 (or_3_out, comparator_24_eq, comparator_25_eq);
  or or_4 (PCSel, or_2_out, or_3_out);
  Comparator #(.width(7)) comparator_26 (.a(Instruction[6:0]), .b(7'b0000011));  // open: gt, eq, lt
  Comparator #(.width(7)) comparator_27 (.a(Instruction[6:0]), .b(7'b1101111));  // open: gt, eq, lt
  Comparator #(.width(7)) comparator_28 (.a(Instruction[6:0]), .b(7'b1100111));  // open: gt, eq, lt
  Comparator #(.width(7)) comparator_29 (.a(Instruction[6:0]), .b(7'b0110011), .eq(comparator_29_eq));  // open: gt, lt
  Comparator #(.width(7)) comparator_30 (.a(Instruction[6:0]), .b(7'b0010011), .eq(comparator_30_eq));  // open: gt, lt
  Comparator #(.width(7)) comparator_31 (.a(Instruction[6:0]), .b(7'b0110011), .eq(comparator_31_eq));  // open: gt, lt
  Comparator #(.width(3)) comparator_32 (.a(Instruction[14:12]), .b(3'b000), .eq(comparator_32_eq));  // open: gt, lt
  Comparator #(.width(7)) comparator_33 (
    .a(Instruction[31:25]), .b(7'b0100000), .eq(comparator_33_eq));  // open: gt, lt
  Comparator #(.width(3)) comparator_34 (.a(Instruction[14:12]), .b(3'b101), .eq(comparator_34_eq));  // open: gt, lt
  Comparator #(.width(7)) comparator_35 (
    .a(Instruction[31:25]), .b(7'b0100000), .eq(comparator_35_eq));  // open: gt, lt
  or or_5 (or_5_out, comparator_29_eq, comparator_30_eq);
  and and_10 (is_sub, comparator_31_eq, comparator_32_eq, comparator_33_eq);
  and and_11 (is_sra, comparator_34_eq, comparator_35_eq);
  Multiplexer #(.enable("false"), .width(4)) multiplexer_7 (.in0(4'b0000), .in1(RISel), .out(ALUSel), .sel(or_5_out));

  // Other names for the same wires on the sheet: opcode[6:0] = Instruction[6:0]; rd[4:0] = Instruction[11:7];
  //   funct3[2:0] = Instruction[14:12]; rs1[4:0] = Instruction[19:15]; rs2[4:0] = Instruction[24:20];
  //   funct7[6:0] = Instruction[31:25]

  // Notes on the sheet:
  //   add
  //   sll
  //   slt
  //   xor
  //   slr
  //   or
  //   and
  //   Branch
  //   beq
  //   bnq
  //   blt
  //   bltu
  //   bge
  //   bgeu
  //   INPUTS to your circuit
  //   R-type
  //   I-type
  //   U-type
  //   J-type
  //   RegWEn
  //   jalr
  //   jal
  //   func3 value correspond to these command directly
  //   PCSel(0->PC+4, 1->ALU)
  //   DON'T CHANGE THE LOCATIONS OF THE INPUTS AND OUTPUTS!
  //   ALUSel
  //   We separately identify the command mul, mulh, mulhu, sub and sra
  //   OUTPUT from your circuit
  //   BSel(0->rs2, 1->imm)
  //   R-Instruction
  //   I-Instruction
  //   ASel(0->rs1, 1->PC)
  //   Decode
  //   Except R and I instructions, other instruction all use add
endmodule
